// Digital circuit alu-32b-final.dig as structural Verilog
module alu_32b_final (
  input  [31:0] A,
  input  [31:0] B,
  input  [7:0] Opcode,
  input  [3:0] control,
  input  [31:0] C,
  input  [1:0] csel,
  input  FLAG_C,
  input  CLK,
  input  FLAG_WE,
  output [31:0] Out,
  output nZout,
  output Zout,
  output Vout,
  output Nout,
  output Bout,
  output Cout,
  output nN,
  output GT_sign,
  output LT_sign,
  output GTE_sign,
  output LTE_sign,
  output nVout,
  output [11:0] CSR_FLAG
);

  wire _74377_2_pin1, ceff0, cin_sel, cout1, cout8, cout16, cout24, g0, g8, g16, g24, g_out_0, g_out_1,
       g_out_2, g_out_3, g_out_4, g_out_5, g_out_6, g_out_7, g_out_A, g_out_B, gb0, gb1, gb2, gb3, gb4, gb5,
       gb6, gb7, gb8, gb9, gb10, gb11, gb12, gb13, gb14, gb15, gb16, gb17, gb18, gb19, gb20, gb21, gb22,
       gb23, gb24, gb25, gb26, gb27, gb28, gb29, gb30, gb31, not_1_out, p0, p8, p16, p24, p_out_0, p_out_1,
       p_out_2, p_out_3, p_out_4, p_out_5, p_out_6, p_out_7, p_out_A, p_out_B, pb0, pb1, pb2, pb3, pb4, pb5,
       pb6, pb7, pb8, pb9, pb10, pb11, pb12, pb13, pb14, pb15, pb16, pb17, pb18, pb19, pb20, pb21, pb22,
       pb23, pb24, pb25, pb26, pb27, pb28, pb29, pb30, pb31, q12, q13, q14, q15, z0, z1, z2, z3, z4, z5, z6,
       z7;
  wire [6:1] cout1_7;
  wire [7:0] ceff8_15, ceff16_23, ceff24_31;
  wire [7:1] ceff0_7, cout8_15, cout16_23, cout24_31, g0_7, g8_15, g16_23, g24_31, p0_7, p8_15, p16_23,
       p24_31;

  _74540 _74540_1 (
    .pin1(1'b0), .pin2(g0), .pin3(g0_7[1]), .pin4(g0_7[2]), .pin5(g0_7[3]), .pin6(g0_7[4]), .pin7(g0_7[5]),
    .pin8(g0_7[6]), .pin9(g0_7[7]), .pin10(1'b0), .pin11(gb7), .pin12(gb6), .pin13(gb5), .pin14(gb4),
    .pin15(gb3), .pin16(gb2), .pin17(gb1), .pin18(gb0), .pin19(1'b0), .pin20(1'b1));
  _74540 _74540_2 (
    .pin1(1'b0), .pin2(p0), .pin3(p0_7[1]), .pin4(p0_7[2]), .pin5(p0_7[3]), .pin6(p0_7[4]), .pin7(p0_7[5]),
    .pin8(p0_7[6]), .pin9(p0_7[7]), .pin10(1'b0), .pin11(pb7), .pin12(pb6), .pin13(pb5), .pin14(pb4),
    .pin15(pb3), .pin16(pb2), .pin17(pb1), .pin18(pb0), .pin19(1'b0), .pin20(1'b1));
  _74540 _74540_3 (
    .pin1(1'b0), .pin2(g8), .pin3(g8_15[1]), .pin4(g8_15[2]), .pin5(g8_15[3]), .pin6(g8_15[4]),
    .pin7(g8_15[5]), .pin8(g8_15[6]), .pin9(g8_15[7]), .pin10(1'b0), .pin11(gb15), .pin12(gb14),
    .pin13(gb13), .pin14(gb12), .pin15(gb11), .pin16(gb10), .pin17(gb9), .pin18(gb8), .pin19(1'b0),
    .pin20(1'b1));
  _74540 _74540_4 (
    .pin1(1'b0), .pin2(p8), .pin3(p8_15[1]), .pin4(p8_15[2]), .pin5(p8_15[3]), .pin6(p8_15[4]),
    .pin7(p8_15[5]), .pin8(p8_15[6]), .pin9(p8_15[7]), .pin10(1'b0), .pin11(pb15), .pin12(pb14),
    .pin13(pb13), .pin14(pb12), .pin15(pb11), .pin16(pb10), .pin17(pb9), .pin18(pb8), .pin19(1'b0),
    .pin20(1'b1));
  _74540 _74540_5 (
    .pin1(1'b0), .pin2(g16), .pin3(g16_23[1]), .pin4(g16_23[2]), .pin5(g16_23[3]), .pin6(g16_23[4]),
    .pin7(g16_23[5]), .pin8(g16_23[6]), .pin9(g16_23[7]), .pin10(1'b0), .pin11(gb23), .pin12(gb22),
    .pin13(gb21), .pin14(gb20), .pin15(gb19), .pin16(gb18), .pin17(gb17), .pin18(gb16), .pin19(1'b0),
    .pin20(1'b1));
  _74540 _74540_6 (
    .pin1(1'b0), .pin2(p16), .pin3(p16_23[1]), .pin4(p16_23[2]), .pin5(p16_23[3]), .pin6(p16_23[4]),
    .pin7(p16_23[5]), .pin8(p16_23[6]), .pin9(p16_23[7]), .pin10(1'b0), .pin11(pb23), .pin12(pb22),
    .pin13(pb21), .pin14(pb20), .pin15(pb19), .pin16(pb18), .pin17(pb17), .pin18(pb16), .pin19(1'b0),
    .pin20(1'b1));
  and and_1 (cin_sel, csel[0], csel[1]);
  Multiplexer #(.Selector_Bits(2)) multiplexer_1 (
    .sel(csel), .in_0(1'b0), .in_1(1'b1), .in_2(FLAG_C), .in_3(C[0]), .out(ceff0));
  Multiplexer #(.Bits(7)) multiplexer_2 (.sel(cin_sel), .in_0({cout1_7, cout1}), .in_1(C[7:1]), .out(ceff0_7));
  Multiplexer #(.Bits(8)) multiplexer_3 (.sel(cin_sel), .in_0({cout8_15, cout8}), .in_1(C[15:8]), .out(ceff8_15));
  Multiplexer #(.Bits(8)) multiplexer_4 (.sel(cin_sel), .in_0({cout16_23, cout16}), .in_1(C[23:16]), .out(ceff16_23));
  Multiplexer #(.Bits(8)) multiplexer_5 (.sel(cin_sel), .in_0({cout24_31, cout24}), .in_1(C[31:24]), .out(ceff24_31));
  _74540 _74540_7 (
    .pin1(1'b0), .pin2(g24), .pin3(g24_31[1]), .pin4(g24_31[2]), .pin5(g24_31[3]), .pin6(g24_31[4]),
    .pin7(g24_31[5]), .pin8(g24_31[6]), .pin9(g24_31[7]), .pin10(1'b0), .pin11(gb31), .pin12(gb30),
    .pin13(gb29), .pin14(gb28), .pin15(gb27), .pin16(gb26), .pin17(gb25), .pin18(gb24), .pin19(1'b0),
    .pin20(1'b1));
  _74540 _74540_8 (
    .pin1(1'b0), .pin2(p24), .pin3(p24_31[1]), .pin4(p24_31[2]), .pin5(p24_31[3]), .pin6(p24_31[4]),
    .pin7(p24_31[5]), .pin8(p24_31[6]), .pin9(p24_31[7]), .pin10(1'b0), .pin11(pb31), .pin12(pb30),
    .pin13(pb29), .pin14(pb28), .pin15(pb27), .pin16(pb26), .pin17(pb25), .pin18(pb24), .pin19(1'b0),
    .pin20(1'b1));
  _74182 _74182_1 (
    .pin1(gb1), .pin2(pb1), .pin3(gb0), .pin4(pb0), .pin5(gb3), .pin6(pb3), .pin7(p_out_0), .pin8(1'b0),
    .pin9(cout1_7[2]), .pin10(g_out_0), .pin11(cout1_7[1]), .pin12(cout1), .pin13(ceff0), .pin14(gb2),
    .pin15(pb2), .pin16(1'b1));
  _74182 _74182_2 (
    .pin1(gb17), .pin2(pb17), .pin3(gb16), .pin4(pb16), .pin5(gb19), .pin6(pb19), .pin7(p_out_4),
    .pin8(1'b0), .pin9(cout16_23[3]), .pin10(g_out_4), .pin11(cout16_23[2]), .pin12(cout16_23[1]),
    .pin13(cout16), .pin14(gb18), .pin15(pb18), .pin16(1'b1));
  _74182 _74182_3 (
    .pin1(gb5), .pin2(pb5), .pin3(gb4), .pin4(pb4), .pin5(gb7), .pin6(pb7), .pin7(p_out_1), .pin8(1'b0),
    .pin9(cout1_7[6]), .pin10(g_out_1), .pin11(cout1_7[5]), .pin12(cout1_7[4]), .pin13(cout1_7[3]),
    .pin14(gb6), .pin15(pb6), .pin16(1'b1));
  _74182 _74182_4 (
    .pin1(gb21), .pin2(pb21), .pin3(gb20), .pin4(pb20), .pin5(gb23), .pin6(pb23), .pin7(p_out_5),
    .pin8(1'b0), .pin9(cout16_23[7]), .pin10(g_out_5), .pin11(cout16_23[6]), .pin12(cout16_23[5]),
    .pin13(cout16_23[4]), .pin14(gb22), .pin15(pb22), .pin16(1'b1));
  _74182 _74182_5 (
    .pin1(gb9), .pin2(pb9), .pin3(gb8), .pin4(pb8), .pin5(gb11), .pin6(pb11), .pin7(p_out_2), .pin8(1'b0),
    .pin9(cout8_15[3]), .pin10(g_out_2), .pin11(cout8_15[2]), .pin12(cout8_15[1]), .pin13(cout8),
    .pin14(gb10), .pin15(pb10), .pin16(1'b1));
  _74182 _74182_6 (
    .pin1(gb25), .pin2(pb25), .pin3(gb24), .pin4(pb24), .pin5(gb27), .pin6(pb27), .pin7(p_out_6),
    .pin8(1'b0), .pin9(cout24_31[3]), .pin10(g_out_6), .pin11(cout24_31[2]), .pin12(cout24_31[1]),
    .pin13(cout24), .pin14(gb26), .pin15(pb26), .pin16(1'b1));
  // alu_8b_final Cell_0: pin names not known; wires that end beside it: Opcode, control[0], A[7:0], B[7:0], {ceff0_7, ceff0}, control[1], control[2], control[3], Out[7:0], {p0_7, p0}, {g0_7, g0}
  // alu_8b_final Cell_1: pin names not known; wires that end beside it: Opcode, control[0], A[15:8], B[15:8], ceff8_15, control[1], control[2], control[3], Out[15:8], {p8_15, p8}, {g8_15, g8}
  _74182 _74182_7 (
    .pin1(gb13), .pin2(pb13), .pin3(gb12), .pin4(pb12), .pin5(gb15), .pin6(pb15), .pin7(p_out_3),
    .pin8(1'b0), .pin9(cout8_15[7]), .pin10(g_out_3), .pin11(cout8_15[6]), .pin12(cout8_15[5]),
    .pin13(cout8_15[4]), .pin14(gb14), .pin15(pb14), .pin16(1'b1));
  _74182 _74182_8 (
    .pin1(gb29), .pin2(pb29), .pin3(gb28), .pin4(pb28), .pin5(gb31), .pin6(pb31), .pin7(p_out_7),
    .pin8(1'b0), .pin9(cout24_31[7]), .pin10(g_out_7), .pin11(cout24_31[6]), .pin12(cout24_31[5]),
    .pin13(cout24_31[4]), .pin14(gb30), .pin15(pb30), .pin16(1'b1));
  // alu_8b_final Cell_2: pin names not known; wires that end beside it: Opcode, control[0], A[23:16], B[23:16], ceff16_23, control[1], control[2], control[3], Out[23:16], {p16_23, p16}, {g16_23, g16}
  // alu_8b_final Cell_3: pin names not known; wires that end beside it: Opcode, control[0], A[31:24], B[31:24], ceff24_31, control[1], control[2], control[3], {Nout, Out[30:24]}, {p24_31, p24}, {g24_31, g24}
  _74182 _74182_9 (
    .pin1(g_out_1), .pin2(p_out_1), .pin3(g_out_0), .pin4(p_out_0), .pin5(g_out_3), .pin6(p_out_3),
    .pin7(p_out_A), .pin8(1'b0), .pin9(cout8_15[4]), .pin10(g_out_A), .pin11(cout8), .pin12(cout1_7[3]),
    .pin13(ceff0), .pin14(g_out_2), .pin15(p_out_2), .pin16(1'b1));
  _74182 _74182_10 (
    .pin1(g_out_5), .pin2(p_out_5), .pin3(g_out_4), .pin4(p_out_4), .pin5(g_out_7), .pin6(p_out_7),
    .pin7(p_out_B), .pin8(1'b0), .pin9(cout24_31[4]), .pin10(g_out_B), .pin11(cout24), .pin12(cout16_23[4]),
    .pin13(cout16), .pin14(g_out_6), .pin15(p_out_6), .pin16(1'b1));
  _74182 _74182_11 (
    .pin1(g_out_B), .pin2(p_out_B), .pin3(g_out_A), .pin4(p_out_A), .pin5(1'b0), .pin6(1'b0), .pin8(1'b0),
    .pin11(Cout), .pin12(cout16), .pin13(ceff0), .pin14(1'b0), .pin15(1'b0), .pin16(1'b1));  // open: pin7, pin9, pin10
  _7425 _7425_1 (
    .pin1(Out[0]), .pin2(Out[1]), .pin3(1'b1), .pin4(Out[2]), .pin5(Out[3]), .pin6(z0), .pin7(1'b0),
    .pin8(z1), .pin9(Out[4]), .pin10(Out[5]), .pin11(1'b1), .pin12(Out[6]), .pin13(Out[7]), .pin14(1'b1));
  _7425 _7425_2 (
    .pin1(Out[16]), .pin2(Out[17]), .pin3(1'b1), .pin4(Out[18]), .pin5(Out[19]), .pin6(z4), .pin7(1'b0),
    .pin8(z5), .pin9(Out[20]), .pin10(Out[21]), .pin11(1'b1), .pin12(Out[22]), .pin13(Out[23]), .pin14(1'b1));
  _7425 _7425_3 (
    .pin1(Out[8]), .pin2(Out[9]), .pin3(1'b0), .pin4(1'b1), .pin5(Out[11]), .pin6(z2), .pin7(1'b0),
    .pin8(z3), .pin9(Out[12]), .pin10(Out[13]), .pin11(1'b1), .pin12(Out[14]), .pin13(Out[15]), .pin14(1'b1));
  _7425 _7425_4 (
    .pin1(Out[24]), .pin2(Out[25]), .pin3(1'b1), .pin4(Out[26]), .pin5(Out[27]), .pin6(z6), .pin7(1'b0),
    .pin8(z7), .pin9(Out[28]), .pin10(Out[29]), .pin11(1'b1), .pin12(Out[30]), .pin13(Nout), .pin14(1'b1));
  _74133 _74133_1 (
    .pin1(z0), .pin2(z1), .pin3(z2), .pin4(z3), .pin5(z4), .pin6(z5), .pin7(z6), .pin8(1'b0), .pin9(nZout),
    .pin10(1'b1), .pin11(1'b1), .pin12(1'b1), .pin13(1'b1), .pin14(z7), .pin15(1'b1), .pin16(1'b1));
  not not_1 (not_1_out, FLAG_WE);
  _74377 _74377_1 (
    .pin1(not_1_out), .pin2(CSR_FLAG[0]), .pin3(Zout), .pin4(nZout), .pin5(CSR_FLAG[1]), .pin6(CSR_FLAG[2]),
    .pin7(Nout), .pin8(nN), .pin9(CSR_FLAG[3]), .pin10(1'b0), .pin11(CLK), .pin12(CSR_FLAG[4]), .pin13(Cout),
    .pin14(Bout), .pin15(CSR_FLAG[5]), .pin16(CSR_FLAG[6]), .pin17(Vout), .pin18(nVout), .pin19(CSR_FLAG[7]),
    .pin20(1'b1));
  not not_2 (nVout, Vout);
  not not_3 (Zout, nZout);
  xor xor_1 (Vout, cout24_31[7], Cout);
  not not_4 (Bout, Cout);
  and and_2 (GT_sign, nZout, GTE_sign);
  or or_1 (LTE_sign, Zout, LT_sign);
  _74377 _74377_2 (
    .pin1(_74377_2_pin1), .pin2(CSR_FLAG[8]), .pin3(LT_sign), .pin4(LTE_sign), .pin5(CSR_FLAG[9]),
    .pin6(CSR_FLAG[10]), .pin7(GT_sign), .pin8(GTE_sign), .pin9(CSR_FLAG[11]), .pin10(1'b0), .pin11(CLK),
    .pin12(q12), .pin13(1'b0), .pin14(1'b0), .pin15(q13), .pin16(q14), .pin17(1'b0), .pin18(1'b0),
    .pin19(q15), .pin20(1'b1));
  not not_5 (_74377_2_pin1, FLAG_WE);
  not not_6 (nN, Nout);
  not not_7 (GTE_sign, LT_sign);
  xor xor_2 (LT_sign, Vout, Nout);

  assign Out[31] = Nout;

  // Other names for the same wires on the sheet: a0_7[7:0] = A[7:0]; a8_15[7:0] = A[15:8]; a16_23[7:0] = A[23:16];
  //   a24_31[7:0] = A[31:24]; b0_7[7:0] = B[7:0]; b8_15[7:0] = B[15:8]; b16_23[7:0] = B[23:16];
  //   b24_31[7:0] = B[31:24]; C_logic[31:0] = C; cin0 = C[0]; c1_7[6:0] = C[7:1]; c8_15[7:0] = C[15:8];
  //   c16_23[7:0] = C[23:16]; c24_31[7:0] = C[31:24]; ceff0_7[0] = ceff0; ceff1_7[6:0] = ceff0_7; asel = control[0];
  //   ainv = control[1]; bsel = control[2]; binv = control[3]; cout1_7[0] = cout1; cout2 = cout1_7[1];
  //   cout3 = cout1_7[2]; cout4 = cout1_7[3]; cout5 = cout1_7[4]; cout6 = cout1_7[5]; cout7 = cout1_7[6];
  //   cout8_15[0] = cout8; cout9 = cout8_15[1]; cout10 = cout8_15[2]; cout11 = cout8_15[3]; cout12 = cout8_15[4];
  //   cout13 = cout8_15[5]; cout14 = cout8_15[6]; cout15 = cout8_15[7]; cout16_23[0] = cout16; cout17 = cout16_23[1];
  //   cout18 = cout16_23[2]; cout19 = cout16_23[3]; cout20 = cout16_23[4]; cout21 = cout16_23[5];
  //   cout22 = cout16_23[6]; cout23 = cout16_23[7]; cout24_31[0] = cout24; cout25 = cout24_31[1];
  //   cout26 = cout24_31[2]; cout27 = cout24_31[3]; cout28 = cout24_31[4]; cout29 = cout24_31[5];
  //   cout30 = cout24_31[6]; cout31 = cout24_31[7]; C_out = Cout; cout32 = Cout; g0_7[0] = g0; g1 = g0_7[1];
  //   g2 = g0_7[2]; g3 = g0_7[3]; g4 = g0_7[4]; g5 = g0_7[5]; g6 = g0_7[6]; g7 = g0_7[7]; g8_15[0] = g8;
  //   g9 = g8_15[1]; g10 = g8_15[2]; g11 = g8_15[3]; g12 = g8_15[4]; g13 = g8_15[5]; g14 = g8_15[6]; g15 = g8_15[7];
  //   g16_23[0] = g16; g17 = g16_23[1]; g18 = g16_23[2]; g19 = g16_23[3]; g20 = g16_23[4]; g21 = g16_23[5];
  //   g22 = g16_23[6]; g23 = g16_23[7]; g24_31[0] = g24; g25 = g24_31[1]; g26 = g24_31[2]; g27 = g24_31[3];
  //   g28 = g24_31[4]; g29 = g24_31[5]; g30 = g24_31[6]; g31 = g24_31[7]; nC_out = Bout; nN_out = nN; nV_out = nVout;
  //   nZ_out = nZout; out0_7[7:0] = Out[7:0]; out32[31:0] = {Nout, Out[30:0]}; out8_15[7:0] = Out[15:8];
  //   out16_23[7:0] = Out[23:16]; out24_31[7:0] = {Nout, Out[30:24]}; N_out = Nout; out31 = Nout; p0_7[0] = p0;
  //   p1 = p0_7[1]; p2 = p0_7[2]; p3 = p0_7[3]; p4 = p0_7[4]; p5 = p0_7[5]; p6 = p0_7[6]; p7 = p0_7[7]; p8_15[0] = p8;
  //   p9 = p8_15[1]; p10 = p8_15[2]; p11 = p8_15[3]; p12 = p8_15[4]; p13 = p8_15[5]; p14 = p8_15[6]; p15 = p8_15[7];
  //   p16_23[0] = p16; p17 = p16_23[1]; p18 = p16_23[2]; p19 = p16_23[3]; p20 = p16_23[4]; p21 = p16_23[5];
  //   p22 = p16_23[6]; p23 = p16_23[7]; p24_31[0] = p24; p25 = p24_31[1]; p26 = p24_31[2]; p27 = p24_31[3];
  //   p28 = p24_31[4]; p29 = p24_31[5]; p30 = p24_31[6]; p31 = p24_31[7]; q0 = CSR_FLAG[0]; q1 = CSR_FLAG[1];
  //   q2 = CSR_FLAG[2]; q3 = CSR_FLAG[3]; q4 = CSR_FLAG[4]; q5 = CSR_FLAG[5]; q6 = CSR_FLAG[6]; q7 = CSR_FLAG[7];
  //   q8 = CSR_FLAG[8]; q9 = CSR_FLAG[9]; q10 = CSR_FLAG[10]; q11 = CSR_FLAG[11]; V_out = Vout; Z_out = Zout

  // Notes on the sheet:
  //   A: default 9
  //   B: default 20
  //   Opcode: default 150
  //   control: default 13
  //   csel: default 1
endmodule

/* Test case Exhaustive 91 Ops Test:
A nz0 B C Opcode control cin-sel FLAG_C Out vout zout nzout nout cout
0x9E250D03 1 0xECEFE37B 0x888417A5 0x96 5 0 0 0x8B14F07E 0 0 1 1 1
0x922BADB0 0 0x95F628F2 0xBB5D75B8 0x96 5 0 0 0x2821D6A2 1 0 1 0 1
0xC6737B8B 1 0xD30A286E 0x5531AE6D 0x96 5 0 0 0x997DA3F9 0 0 1 1 1
0xA28718E5 1 0xCA2410FD 0x5C1ED35F 0x96 5 0 0 0x6CAB29E2 1 0 1 0 1
0x643CB56D 0 0xFE03E76F 0xB2767375 0x96 5 0 0 0x62409CDC 0 0 1 0 1
0xC2F40B30 1 0xA801CF8B 0xDD23F7B6 0x96 5 0 1 0x6AF5DABC 1 0 1 0 1
0x1BFA530D 1 0x6CECC258 0xD2083355 0x96 5 0 1 0x88E71566 1 0 1 1 0
0xE66EB118 1 0x10BA53D8 0x8161701F 0x96 5 0 1 0xF72904F1 0 0 1 1 0
0xE369AB3D 1 0x67518339 0x67433A86 0x96 5 0 1 0x4ABB2E77 0 0 1 0 1
0xA9EB7262 1 0x0490392A 0xD51F25E6 0x96 5 0 1 0xAE7BAB8D 0 0 1 1 0
0x982E524E 0 0x1E5876BF 0x75FFBFF5 0x96 5 0 1 0xB686C90E 0 0 1 1 0
0xF522DFDC 1 0x2BD4E7AB 0xCBB452AE 0x96 5 0 1 0x20F7C788 0 0 1 0 1
0xADE42791 1 0xB0C751A5 0xEBF96C57 0x96 5 0 1 0x5EAB7937 1 0 1 0 1
0x9A795FF6 0 0x43CD9D75 0xCDD25AA1 0x96 5 0 1 0xDE46FD6C 0 0 1 1 0
0x8C39D6BB 0 0x113A972F 0xA36AEC07 0x96 5 0 1 0x9D746DEB 0 0 1 1 0
0x127E2CC8 0 0x684FF42B 0xF666C60F 0x96 1 0 1 0x127E2CC9 0 0 1 0 0
0xACF40C45 0 0x0463522C 0xA28F38BD 0x96 1 0 1 0xACF40C46 0 0 1 1 0
0x32700980 0 0x1AC66DEA 0x48F0E642 0x96 1 0 1 0x32700981 0 0 1 0 0
0x73CBC7FD 1 0xBFC5C2A1 0xEAA1C37B 0x96 1 0 1 0x73CBC7FE 0 0 1 0 0
0x0330F04D 1 0xCB9FD223 0xEFD6A13E 0x96 1 0 1 0x0330F04E 0 0 1 0 0
0x6EA29BD0 0 0x9275BAB2 0xCA5976A6 0x96 4 0 1 0x9275BAB3 0 0 1 1 0
0x8CB33116 1 0x0BBBAED5 0xC6A7BA53 0x96 4 0 1 0x0BBBAED6 0 0 1 0 0
0xD932B231 0 0xE433713D 0x36B1CC9F 0x96 4 0 1 0xE433713E 0 0 1 1 0
0x8771830D 0 0x86D6B717 0x87485FF5 0x96 4 0 1 0x86D6B718 0 0 1 1 0
0xC67B74E2 1 0xA9A29C4C 0x0CE941CC 0x96 4 0 1 0xA9A29C4D 0 0 1 1 0
0xB421B5BA 1 0xBC8B306F 0x95714C91 0x96 9 0 0 0xB421B5B9 0 0 1 1 1
0xF9307A71 1 0xE6171071 0x0649D0EB 0x96 9 0 0 0xF9307A70 0 0 1 1 1
0x8AD5F511 1 0xC08EEEE9 0xA779CFE5 0x96 9 0 0 0x8AD5F510 0 0 1 1 1
0xBC15526A 1 0x8EF1FB25 0xCC638D6A 0x96 9 0 0 0xBC155269 0 0 1 1 1
0x4303F922 0 0x11190839 0xB5710CDB 0x96 9 0 0 0x4303F921 0 0 1 0 1
0xF2A57B17 0 0x0F140E3F 0xE7545280 0x96 6 0 0 0x0F140E3E 0 0 1 0 1
0x50E84FEE 0 0xD1EA37FC 0x1413B58C 0x96 6 0 0 0xD1EA37FB 0 0 1 1 1
0x70806354 1 0xF3E1F4FC 0x8A59AED2 0x96 6 0 0 0xF3E1F4FB 0 0 1 1 1
0xE0A94677 0 0x0DBBFF09 0x8DF6073D 0x96 6 0 0 0x0DBBFF08 0 0 1 0 1
0x6D53855D 0 0x59667DF9 0x9B3C8F00 0x96 6 0 0 0x59667DF8 0 0 1 0 1
0x6E10D8AC 0 0x4999DEE8 0xBDB78C3F 0x96 3 0 1 0x91EF2754 0 0 1 1 0
0x0E531C17 1 0xA24898EF 0x7618F5FD 0x96 3 0 1 0xF1ACE3E9 0 0 1 1 0
0x6164B99C 1 0x118344EB 0x355AC876 0x96 3 0 1 0x9E9B4664 0 0 1 1 0
0xA83BC84C 1 0xAD46E79A 0xA4CC68AA 0x96 3 0 1 0x57C437B4 0 0 1 0 0
0xB7A60EC1 0 0x36B87E69 0x310791BB 0x96 3 0 1 0x4859F13F 0 0 1 0 0
0x7BEBC774 1 0x6451FADD 0x9CF8D97F 0x96 12 0 1 0x9BAE0523 0 0 1 1 0
0x8D85B315 0 0x40BC0884 0x28E3D333 0x96 12 0 1 0xBF43F77C 0 0 1 1 0
0xB61E20F7 1 0xFDC95E56 0xD7B9BA35 0x96 12 0 1 0x0236A1AA 0 0 1 0 0
0x649866E0 1 0x9FD67893 0x31CCDCBD 0x96 12 0 1 0x6029876D 0 0 1 0 0
0xEF320F9E 1 0x28BA4DB2 0xB7C8CF35 0x96 12 0 1 0xD745B24E 0 0 1 1 0
0x9F39D060 1 0xB29983BC 0xA111B92E 0x96 3 0 0 0x60C62F9F 0 0 1 0 0
0x0A14680D 0 0x07BD9483 0x8A3B319F 0x96 3 0 0 0xF5EB97F2 0 0 1 1 0
0xA42CA3E6 1 0x6FFEDC96 0x4E939F7B 0x96 3 0 0 0x5BD35C19 0 0 1 0 0
0xC7E29A0A 1 0x670370E8 0xDFBE3B62 0x96 3 0 0 0x381D65F5 0 0 1 0 0
0x399FCFD6 1 0xEAD13C41 0x4E26B0B8 0x96 3 0 0 0xC6603029 0 0 1 1 0
0x9483F548 1 0x6109DFB9 0xF7375D41 0x96 12 0 0 0x9EF62046 0 0 1 1 0
0x24E1BA2D 1 0x9FA88BBA 0xD202751C 0x96 12 0 0 0x60577445 0 0 1 0 0
0xC339627C 1 0xBF0D1338 0x3C9921ED 0x96 12 0 0 0x40F2ECC7 0 0 1 0 0
0xD02819D9 1 0xB556EC05 0x15F909CC 0x96 12 0 0 0x4AA913FA 0 0 1 0 0
0xB1AC56A2 0 0x00BC9D0C 0x57ADF7DB 0x96 12 0 0 0xFF4362F3 0 0 1 1 0
0xD75CE2E2 1 0xEE87E8A2 0x4674252D 0x96 1 0 0 0xD75CE2E2 0 0 1 1 0
0x86F40248 1 0xD1CC2302 0x981D1BAA 0x96 1 0 0 0x86F40248 0 0 1 1 0
0xFF195E1B 1 0x23B8EF17 0x0982694D 0x96 1 0 0 0xFF195E1B 0 0 1 1 0
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*/
