// Digital circuit alu-8b-final.dig as structural Verilog
module alu_8b_final (
  input  [7:0] lutA,
  input  [7:0] A,
  input  [7:0] B,
  input  [7:0] C,
  input  [7:0] lutB,
  input  zin,
  input  FLAG_WE,
  input  [2:0] csel,
  input  CLK,
  output [7:0] out,
  output [7:0] csr_flg,
  output zout,
  output cout
);

  wire _7400_1_pin3, _7400_1_pin9, _7400_2_pin3, _74377_1_pin1, Aeff, Beff, c0, CIN_MAIN, GT_sign, GTE_sign,
       j0, j1, LT_sign, nZout, V_out, xC;

  alu_4b_final alu_4b_final_1 (
    .A(A[3:0]), .B(B[3:0]), .lutA(lutA), .C(C[3:0]), .cin(CIN_MAIN), .lutB(lutB), .Out(out[3:0]), .cout(c0));  // open: aeff3, beff3
  // alu_4b_final alu_4b_final_2: pin names not known; wires that end beside it: A[7:4], B[7:4], lutA, C[7:4], c0, lutB, out[7:4], cout, Aeff, Beff
  _7400 _7400_1 (
    .pin1(nZout), .pin2(GTE_sign), .pin3(_7400_1_pin3), .pin4(_7400_1_pin3), .pin5(_7400_1_pin3),
    .pin6(GT_sign), .pin7(1'b0), .pin8(V_out), .pin9(_7400_1_pin9), .pin10(_7400_1_pin9),
    .pin11(_7400_1_pin9), .pin12(j1), .pin13(j0), .pin14(1'b1));
  _74377 _74377_1 (
    .pin1(_74377_1_pin1), .pin2(csr_flg[0]), .pin3(zout), .pin4(nZout), .pin5(csr_flg[1]), .pin6(csr_flg[2]),
    .pin7(out[7]), .pin8(cout), .pin9(csr_flg[3]), .pin10(1'b0), .pin11(CLK), .pin12(csr_flg[4]),
    .pin13(V_out), .pin14(LT_sign), .pin15(csr_flg[5]), .pin16(csr_flg[6]), .pin17(GT_sign),
    .pin18(GTE_sign), .pin19(csr_flg[7]), .pin20(1'b1));
  not not_1 (_74377_1_pin1, FLAG_WE);
  _7400 _7400_2 (
    .pin1(nZout), .pin2(nZout), .pin3(_7400_2_pin3), .pin4(_7400_2_pin3), .pin5(zin), .pin6(xC), .pin7(1'b0),
    .pin8(zout), .pin9(xC), .pin10(xC), .pin12(1'b0), .pin13(1'b0), .pin14(1'b1));  // open: pin11
  _74151 _74151_1 (
    .pin1(csr_flg[0]), .pin2(csr_flg[2]), .pin3(1'b1), .pin4(1'b0), .pin5(CIN_MAIN), .pin7(1'b0),
    .pin8(1'b0), .pin9(csel[2]), .pin10(csel[1]), .pin11(csel[0]), .pin12(csr_flg[4]), .pin13(csr_flg[5]),
    .pin14(csr_flg[6]), .pin15(csr_flg[3]), .pin16(1'b1));  // open: pin6
  _7486 _7486_1 (
    .pin1(Aeff), .pin2(out[7]), .pin3(j0), .pin4(out[7]), .pin5(Beff), .pin6(j1), .pin7(1'b0),
    .pin8(GTE_sign), .pin9(LT_sign), .pin10(LT_sign), .pin11(LT_sign), .pin12(V_out), .pin13(out[7]),
    .pin14(1'b1));
  _74688 _74688_1 (
    .pin1(1'b0), .pin2(out[0]), .pin3(1'b0), .pin4(out[1]), .pin5(1'b0), .pin6(out[2]), .pin7(1'b0),
    .pin8(out[3]), .pin9(1'b0), .pin10(1'b0), .pin11(out[4]), .pin12(1'b0), .pin13(out[5]), .pin14(1'b0),
    .pin15(out[6]), .pin16(1'b0), .pin17(out[7]), .pin18(1'b0), .pin19(nZout), .pin20(1'b1));

  // Other names for the same wires on the sheet: A_3__0[3:0] = A[3:0]; A_7__4[3:0] = A[7:4]; B_3__0[3:0] = B[3:0];
  //   B_7__4[3:0] = B[7:4]; C_3__0[3:0] = C[3:0]; C_7__4[3:0] = C[7:4]; COUT_MAIN = cout; cin_SEL_0 = csel[0];
  //   cin_SEL_1 = csel[1]; cin_SEL_2 = csel[2]; flag_c = csr_flg[3]; flag_gt = csr_flg[6]; flag_gte = csr_flg[7];
  //   flag_lt = csr_flg[5]; flag_n = csr_flg[2]; flag_v = csr_flg[4]; flag_z = csr_flg[0]; flag_z_b = csr_flg[1];
  //   OUT_4[3:0] = out[3:0]; OUT_8[3:0] = out[7:4]; Z_out = zout

  // Notes on the sheet:
  //   lutA: default 170
  //   A: default 6
  //   B: default 1
  //   C: default 1
  //   lutB: default 204
  //   FLAG_WE: default 1
  //   CLK: Hz: 100
endmodule
