// Digital circuit main.dig as structural Verilog
module main (
  input  clk,
  input  reset,
  input  [7:0] kb_data,
  input  [12:0] disp_read,
  input  kb_en,
  output [23:0] pc_out,
  output [31:0] mem_din,
  output [31:0] ir_bus,
  output [21:0] ir_offset,
  output [21:0] ir_addr,
  output [5:0] ir_addr_w,
  output [5:0] ir_addr_b,
  output [2:0] wb_sel,
  output [9:0] ir_opcode,
  output [7:0] ctrl_alu_op,
  output [31:0] alu_out,
  output [31:0] reg_w_data,
  output [23:0] pc_save,
  output [31:0] m_out,
  output [23:0] mem_addr,
  output [2:0] ctrl_w_sel,
  output [31:0] reg_b,
  output [31:0] reg_a,
  output ctrl_reg_we,
  output [5:0] ir_addr_a,
  output [3:0] ir_sel,
  output [31:0] disp_out,
  output [23:0] pc_link
);

  wire BANK_SEL, csr_flags, ctrl_bank_en, ctrl_branch_en, ctrl_enc, ctrl_flags_we, ctrl_jump_type,
       ctrl_mem_rd, ctrl_mem_wr, ctrl_mul_div_en, ctrl_pc_link_WE, HALT_IN, mem_rd_out, nflag_A_zero, reg_c,
       seq_exec, seq_fetch;
  wire [1:0] ctrl_cin_sel, ctrl_cycles, ctrl_shift_op, ctrl_sp_out;
  wire [2:0] ctrl_bus_sel, ctrl_pc_cond, ctrl_pc_src;
  wire [3:0] ctrl_alu_pre, ctrl_byte_sel;
  wire [15:0] mul_nxt_enc;
  wire [23:0] sp_out;
  wire [31:0] shift_mul_p_enc;

  alu_control alu_control_1 (.op(ir_opcode), .alu_op(ctrl_alu_op), .alu_pre(ctrl_alu_pre), .cin_sel(ctrl_cin_sel));
  ir_reg_control ir_reg_control_1 (.op(ir_opcode), .ir_imm_sel(ir_sel), .wb_sel(ctrl_w_sel), .reg_we(ctrl_reg_we));
  mem_bus_control mem_bus_control_1 (.op(ir_opcode), .ctrl_bussel(ctrl_bus_sel));
  // mem_io_control mem_io_control_1: pin names not known; wires that end beside it: ir_opcode, ctrl_bank_en, ctrl_flags_we, ctrl_mem_rd, ctrl_mem_wr, ctrl_byte_sel
  pc_control pc_control_1 (
    .op(ir_opcode), .exec(seq_exec), .branch_en(ctrl_branch_en), .jump_type(ctrl_jump_type),
    .pc_src(ctrl_pc_src), .pc_link_we(ctrl_pc_link_WE), .cycles(ctrl_cycles), .pc_cond(ctrl_pc_cond),
    .sp_out(ctrl_sp_out), .HALT_IN(HALT_IN));
  shift_mul_control shift_mul_control_1 (
    .op(ir_opcode), .shift_op(ctrl_shift_op), .mul_div_en(ctrl_mul_div_en), .pc_enc(ctrl_enc));
  // alu_32b_final alu_32b_final_1: pin names not known; wires that end beside it: reg_a, ir_bus, ctrl_alu_op, ctrl_alu_pre, reg_c, ctrl_cin_sel, clk, ctrl_flags_we, nflag_A_zero, alu_out, csr_flags
  // register register_1: pin names not known; wires that end beside it: ctrl_reg_we, reg_w_data, ir_addr_a, ir_addr_b, ir_addr_w, seq_exec, clk, BANK_SEL, ctrl_bank_en, reg_a, reg_b, reg_c
  mul_div mul_div_1 (
    .B(ir_bus), .mode(ctrl_shift_op), .mul_div(ctrl_mul_div_en), .A(reg_a), .p_enc(ctrl_enc),
    .Out(shift_mul_p_enc), .nflag_A_is_Z(nflag_A_zero), .mul_nxt_enc(mul_nxt_enc));
  vga vga_1 (
    .mem_addr(mem_addr), .mem_din(reg_w_data), .disp_read_addr(disp_read), .clk(clk), .disp_data_out(disp_out));
  // ir ir_1: pin names not known; wires that end beside it: mem_din, seq_fetch, clk, ir_sel, reg_b, ir_opcode, ir_addr_a, ir_addr_b, ir_addr_w, ir_addr, ir_offset, ir_bus, BANK_SEL
  EEPROMDualPort #(.AddrBits(24), .Bits(32)) eepromdualport_1 (
    .A(mem_addr), .Din(reg_w_data), .str(ctrl_mem_wr), .C(clk), .ld(mem_rd_out), .D(m_out));
  byte_lane_decoder byte_lane_decoder_1 (
    .mem_in(m_out), .sel_in(ctrl_byte_sel), .io_data_in(kb_data), .mem_out(mem_din));
  // program_counter program_counter_1: pin names not known; wires that end beside it: mem_din, alu_out, ctrl_pc_src, ir_offset, reset, ctrl_cycles, csr_flags, ctrl_pc_cond, ctrl_jump_type, ctrl_branch_en, 1'b1, HALT_IN, kb_en, 1'b1, 1'b1, 1'b1, ctrl_pc_link_WE, clk, pc_out, pc_save, seq_fetch, seq_exec, pc_link
  sp sp_1 (.sp_op(ctrl_sp_out), .CLK(clk), .Reset(reset), .sp_load_in(alu_out), .seq_exec(seq_exec), .sp_out(sp_out));
  // wb_mux wb_mux_1: pin names not known; wires that end beside it: ctrl_w_sel, alu_out, shift_mul_p_enc, pc_save, mem_din, reg_a, ir_bus, csr_flags, mul_nxt_enc, reg_w_data
  // bus_arbitration bus_arbitration_1: pin names not known; wires that end beside it: seq_fetch, ir_addr, ctrl_mem_rd, ctrl_bus_sel, reg_b, pc_out, sp_out, alu_out, mem_addr, mem_rd_out

  assign wb_sel = ctrl_w_sel;

  // Other names for the same wires on the sheet: ctrl_ir_sel[3:0] = ir_sel; ctrl_wb_sel[2:0] = ctrl_w_sel;
  //   disp_read_addr[12:0] = disp_read; mem_ram_out[31:0] = m_out; wb_data[31:0] = reg_w_data

  // Notes on the sheet:
  //   Control Unit
  //   ALU
  //   Shift - Encoder
  //   Memory
  //   Instruction Register
  //   contents of eepromdualport_1 (hex, n*v repeats v):
  //   4002800,18bfffff
  //   Program Counter
  //   Data Bus Switch
endmodule

/* Test case Trace Execution:
clk reset disp-read kb_en pc-out ir-opcode
0 1 0 0 x x
C 1 0 0 x x
0 0 0 0 999 x
C 0 0 0 x x
0 0 0 0 999 x
C 0 0 0 x x
0 0 0 0 999 x
C 0 0 0 x x
0 0 0 0 999 x
C 0 0 0 x x
0 0 0 0 999 x
C 0 0 0 x x
0 0 0 0 999 x
C 0 0 0 x x
0 0 0 0 999 x
C 0 0 0 x x
0 0 0 0 999 x
C 0 0 0 x x
0 0 0 0 999 x
C 0 0 0 x x
0 0 0 0 999 x
C 0 0 0 x x
0 0 0 0 999 x
C 0 0 0 x x
0 0 0 0 999 x
C 0 0 0 x x
0 0 0 0 999 x
C 0 0 0 x x
0 0 0 0 999 x
C 0 0 0 x x
0 0 0 0 999 x
C 0 0 0 x x
0 0 0 0 999 x
C 0 0 0 x x
0 0 0 0 999 x
C 0 0 0 x x
0 0 0 0 999 x
C 0 0 0 x x
0 0 0 0 999 x
C 0 0 0 x x
0 0 0 0 999 x
C 0 0 0 x x
0 0 0 0 999 x
C 0 0 0 x x
0 0 0 0 999 x
C 0 0 0 x x
0 0 0 0 999 x
C 0 0 0 x x
0 0 0 0 999 x
C 0 0 0 x x
0 0 0 0 999 x
C 0 0 0 x x
0 0 0 0 999 x
C 0 0 0 x x
0 0 0 0 999 x
C 0 0 0 x x
0 0 0 0 999 x
C 0 0 0 x x
0 0 0 0 999 x
C 0 0 0 x x
0 0 0 0 999 x
C 0 0 0 x x
0 0 0 0 999 x
C 0 0 0 x x
0 0 0 0 999 x
C 0 0 0 x x
0 0 0 0 999 x
C 0 0 0 x x
0 0 0 0 999 x
C 0 0 0 x x
0 0 0 0 999 x
C 0 0 0 x x
0 0 0 0 999 x
C 0 0 0 x x
0 0 0 0 999 x
C 0 0 0 x x
0 0 0 0 999 x
C 0 0 0 x x
0 0 0 0 999 x
C 0 0 0 x x
0 0 0 0 999 x
C 0 0 0 x x
0 0 0 0 999 x
C 0 0 0 x x
0 0 0 0 999 x
C 0 0 0 x x
0 0 0 0 999 x
C 0 0 0 x x
0 0 0 0 999 x
C 0 0 0 x x
0 0 0 0 999 x
C 0 0 0 x x
0 0 0 0 999 x
C 0 0 0 x x
0 0 0 0 999 x
C 0 0 0 x x
0 0 0 0 999 x
C 0 0 0 x x
0 0 0 0 999 x
C 0 0 0 x x
0 0 0 0 999 x
C 0 0 0 x x
0 0 0 0 999 x
C 0 0 0 x x
0 0 0 0 999 x
C 0 0 0 x x
0 0 0 0 999 x
C 0 0 0 x x
0 0 0 0 999 x
C 0 0 0 x x
0 0 0 0 999 x
C 0 0 0 x x
0 0 0 0 999 x
C 0 0 0 x x
0 0 0 0 999 x
C 0 0 0 x x
0 0 0 0 999 x
C 0 0 0 x x
0 0 0 0 999 x
C 0 0 0 x x
0 0 0 0 999 x
C 0 0 0 x x
0 0 0 0 999 x
C 0 0 0 x x
0 0 0 0 999 x
C 0 0 0 x x
0 0 0 0 999 x
C 0 0 0 x x
0 0 0 0 999 x
C 0 0 0 x x
0 0 0 0 999 x
C 0 0 0 x x
0 0 0 0 999 x
C 0 0 0 x x
0 0 0 0 999 x
C 0 0 0 x x
0 0 0 0 999 x
C 0 0 0 x x
0 0 0 0 999 x
C 0 0 0 x x
0 0 0 0 999 x
C 0 0 0 x x
0 0 0 0 999 x
C 0 0 0 x x
0 0 0 0 999 x
C 0 0 0 x x
0 0 0 0 999 x
C 0 0 0 x x
0 0 0 0 999 x
C 0 0 0 x x
0 0 0 0 999 x
C 0 0 0 x x
0 0 0 0 999 x
C 0 0 0 x x
0 0 0 0 999 x
C 0 0 0 x x
0 0 0 0 999 x
C 0 0 0 x x
0 0 0 0 999 x
C 0 0 0 x x
0 0 0 0 999 x
C 0 0 0 x x
0 0 0 0 999 x
C 0 0 0 x x
0 0 0 0 999 x
C 0 0 0 x x
0 0 0 0 999 x
C 0 0 0 x x
0 0 0 0 999 x
C 0 0 0 x x
0 0 0 0 999 x
C 0 0 0 x x
0 0 0 0 999 x
C 0 0 0 x x
0 0 0 0 999 x
C 0 0 0 x x
0 0 0 0 999 x
C 0 0 0 x x
0 0 0 0 999 x
C 0 0 0 x x
0 0 0 0 999 x
C 0 0 0 x x
0 0 0 0 999 x
C 0 0 0 x x
0 0 0 0 999 x
C 0 0 0 x x
0 0 0 0 999 x
C 0 0 0 x x
0 0 0 0 999 x
C 0 0 0 x x
0 0 0 0 999 x
C 0 0 0 x x
0 0 0 0 999 x
C 0 0 0 x x
0 0 0 0 999 x
C 0 0 0 x x
0 0 0 0 999 x
C 0 0 0 x x
0 0 0 0 999 x
C 0 0 0 x x
0 0 0 0 999 x
C 0 0 0 x x
0 0 0 0 999 x
C 0 0 0 x x
0 0 0 0 999 x
C 0 0 0 x x
0 0 0 0 999 x
C 0 0 0 x x
0 0 0 0 999 x
C 0 0 0 x x
0 0 0 0 999 x
C 0 0 0 x x
0 0 0 0 999 x
C 0 0 0 x x
0 0 0 0 999 x
C 0 0 0 x x
0 0 0 0 999 x
C 0 0 0 x x
0 0 0 0 999 x
C 0 0 0 x x
0 0 0 0 999 x
C 0 0 0 x x
0 0 0 0 999 x
C 0 0 0 x x
0 0 0 0 999 x
C 0 0 0 x x
0 0 0 0 999 x
C 0 0 0 x x
0 0 0 0 999 x
C 0 0 0 x x
0 0 0 0 999 x
C 0 0 0 x x
0 0 0 0 999 x
C 0 0 0 x x
0 0 0 0 999 x
C 0 0 0 x x
0 0 0 0 999 x
C 0 0 0 x x
0 0 0 0 999 x
C 0 0 0 x x
0 0 0 0 999 x
C 0 0 0 x x
0 0 0 0 999 x
C 0 0 0 x x
0 0 0 0 999 x
C 0 0 0 x x
0 0 0 0 999 x
C 0 0 0 x x
0 0 0 0 999 x
C 0 0 0 x x
0 0 0 0 999 x
C 0 0 0 x x
0 0 0 0 999 x
C 0 0 0 x x
0 0 0 0 999 x
C 0 0 0 x x
0 0 0 0 999 x
C 0 0 0 x x
0 0 0 0 999 x
C 0 0 0 x x
0 0 0 0 999 x
C 0 0 0 x x
0 0 0 0 999 x
C 0 0 0 x x
0 0 0 0 999 x
C 0 0 0 x x
0 0 0 0 999 x
C 0 0 0 x x
0 0 0 0 999 x
C 0 0 0 x x
0 0 0 0 999 x
C 0 0 0 x x
0 0 0 0 999 x
C 0 0 0 x x
0 0 0 0 999 x
C 0 0 0 x x
0 0 0 0 999 x
C 0 0 0 x x
0 0 0 0 999 x
C 0 0 0 x x
0 0 0 0 999 x
C 0 0 0 x x
0 0 0 0 999 x
C 0 0 0 x x
0 0 0 0 999 x
C 0 0 0 x x
0 0 0 0 999 x
C 0 0 0 x x
0 0 0 0 999 x
C 0 0 0 x x
0 0 0 0 999 x
C 0 0 0 x x
0 0 0 0 999 x
C 0 0 0 x x
0 0 0 0 999 x
C 0 0 0 x x
0 0 0 0 999 x
C 0 0 0 x x
0 0 0 0 999 x
C 0 0 0 x x
0 0 0 0 999 x
C 0 0 0 x x
0 0 0 0 999 x
C 0 0 0 x x
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*/
