// Digital circuit microcode.dig as structural Verilog
module microcode (
  input  [7:0] op,
  output [7:0] alu_op,
  output [4:0] alu_pre,
  output cin_sel,
  output [1:0] shift_op,
  output [3:0] ir_imm_sel,
  output addr_csel,
  output [2:0] wb_sel,
  output reg_we,
  output flags_we,
  output mem_rd,
  output mem_wr,
  output [1:0] mem_sel,
  output branch_en,
  output jump_type,
  output [1:0] sp_op,
  output pc_rel,
  output [1:0] cycles,
  output [2:0] ctrl_bussel,
  output mul_en,
  output div_en
);

  wire [47:42] microcode_eeprom_d;

  ROM #(.bigEndian("true"), .AddrBits(8), .Bits(48)) microcode_eeprom (
    .A(op), .sel(1'b1),
    .D({microcode_eeprom_d, div_en, mul_en, ctrl_bussel, cycles, pc_rel, sp_op, jump_type, branch_en, mem_sel, mem_wr, mem_rd, flags_we, reg_we, wb_sel, addr_csel, ir_imm_sel, shift_op, cin_sel, alu_pre, alu_op}));

  // Notes on the sheet:
  //   op: default 48
  //   microcode_eeprom loads microopcode_rom.hex
endmodule

/* Test case:
op alu-op alu-pre cin-sel shift-op ir-imm-sel addr-csel wb-sel reg-we flags-we mem-rd mem-wr mem-sel branch-en jump-type sp-op pc-rel cycles ctrl-bussel mul-en div-en

# TOMATO32 MICROCODE ROM — REFINED
# Format: op alu-op alu-pre cin-sel shift-op ir-imm-sel addr-csel wb-sel reg-we flags-we mem-rd mem-wr mem-sel branch-en jump-type sp-op pc-rel cycles ctrl-bussel mul-en div-en
#
# wb-sel values: 0=alu_out 1=shift_out 2=pc_save 3=mem_din 4=flags 5=reg_a 6=ir-bus 7=mul_lo
# shift-op: 0=LSL 1=LSR 2=ASR 3=ROR
# sp-op: 0=hold 1=+1(pop) 2=-1(push) 3=load
# ctrl-bussel: 0=IR_ADDR 1=ALU_out 2=Reg_B 3=PC 4=spare 5=spare 6=spare 7=SP
# ir-imm-sel: 0=reg_b 1=8b_zero 2=8b_sign 3=12b_sign 4=12b_zero 5=SHAMT 6=5b_width 7=16b_zero 8=16b_sign 9=24b_sign 10=LUI16 11=LUI20 12=18bx4 13=26bx4 14=spare 15=spare
# mem-sel: 0=word 1=byte_sign 2=byte_zero 3=half (addr[1:0] picks lane)

# ============================================================
# GROUP 0x00 — SYSTEM
# ============================================================
# NOP — do nothing, advance PC
0x00 0x00 0x00 0 0 0 0 0 0 0 0 0 0 0 0 0 0 1 0 0 0

# HALT — stop machine (0xFF = special opcode detect)
0xFF 0x00 0x00 0 0 0 0 0 0 0 0 0 0 0 0 0 0 1 0 0 0

# ============================================================
# GROUP 0x01-0x0F — ALU REGISTER OPERATIONS (rd = rA OP rB)
# reg-we=1, flags-we=1, wb-sel=0(alu_out), cycles=1
# ============================================================
# ADD  rd, rA, rB
0x01 0x96 0x05 0 0 0 0 0 1 1 0 0 0 0 0 0 0 1 0 0 0
# SUB  rd, rA, rB
0x02 0x96 0x0D 1 0 0 0 0 1 1 0 0 0 0 0 0 0 1 0 0 0
# AND  rd, rA, rB
0x03 0x88 0x05 0 0 0 0 0 1 1 0 0 0 0 0 0 0 1 0 0 0
# OR   rd, rA, rB
0x04 0xEE 0x05 0 0 0 0 0 1 1 0 0 0 0 0 0 0 1 0 0 0
# XOR  rd, rA, rB
0x05 0x66 0x05 0 0 0 0 0 1 1 0 0 0 0 0 0 0 1 0 0 0
# NOT  rd, rA  (NOT A, B ignored)
0x06 0x33 0x01 0 0 0 0 0 1 1 0 0 0 0 0 0 0 1 0 0 0
# NEG  rd, rA  (~A + 1)
0x07 0x96 0x07 1 0 0 0 0 1 1 0 0 0 0 0 0 0 1 0 0 0
# ADC  rd, rA, rB  (ADD with carry in)
0x08 0x96 0x05 1 0 0 0 0 1 1 0 0 0 0 0 0 0 1 0 0 0
# SBC  rd, rA, rB  (SUB with borrow)
0x09 0x69 0x07 1 0 0 0 0 1 1 0 0 0 0 0 0 0 1 0 0 0
# ANDN rd, rA, rB  (A AND NOT B — BIC)
0x0A 0xC0 0x05 0 0 0 0 0 1 1 0 0 0 0 0 0 0 1 0 0 0
# ORN  rd, rA, rB  (A OR NOT B)
0x0B 0xEE 0x02 0 0 0 0 0 1 1 0 0 0 0 0 0 0 1 0 0 0
# INC  rd, rA  (A + 1)
0x0C 0x96 0x05 1 0 0 0 0 1 1 0 0 0 0 0 0 0 1 0 0 0
# DEC  rd, rA  (A - 1, via A + ~0)
0x0D 0x96 0x0F 0 0 0 0 0 1 1 0 0 0 0 0 0 0 1 0 0 0
# MOV  rd, rB  (pass B through ALU)
0x0E 0xCC 0x04 0 0 0 0 0 1 0 0 0 0 0 0 0 0 1 0 0 0
# CMP  rA, rB  (SUB flags only, no writeback)
0x0F 0x69 0x07 0 0 0 0 0 0 1 0 0 0 0 0 0 0 1 0 0 0

# ============================================================
# GROUP 0x10-0x1F — ALU IMMEDIATE OPERATIONS (rd = rA OP imm)
# ir-imm-sel selects which immediate channel
# ============================================================
# ADDI rd, rA, imm12s  (RV32I style)
0x10 0x96 0x05 0 0 3 0 0 1 1 0 0 0 0 0 0 0 1 0 0 0
# SUBI rd, rA, imm12s
0x11 0x69 0x07 0 0 3 0 0 1 1 0 0 0 0 0 0 0 1 0 0 0
# ANDI rd, rA, imm16z  (MIPS style zero-ext)
0x12 0x88 0x05 0 0 7 0 0 1 1 0 0 0 0 0 0 0 1 0 0 0
# ORI  rd, rA, imm16z
0x13 0xEE 0x05 0 0 7 0 0 1 1 0 0 0 0 0 0 0 1 0 0 0
# XORI rd, rA, imm16z
0x14 0x66 0x05 0 0 7 0 0 1 1 0 0 0 0 0 0 0 1 0 0 0
# ADDI rd, rA, imm16s  (PPC/MIPS style)
0x15 0x96 0x05 0 0 8 0 0 1 1 0 0 0 0 0 0 0 1 0 0 0
# ADDI rd, rA, imm8s   (SH-2/68k style)
0x16 0x96 0x05 0 0 2 0 0 1 1 0 0 0 0 0 0 0 1 0 0 0
# TST  rA, imm  (AND flags only)
0x17 0x88 0x05 0 0 7 0 0 0 1 0 0 0 0 0 0 0 1 0 0 0
# CMPI rA, imm12s
0x18 0x69 0x07 0 0 3 0 0 0 1 0 0 0 0 0 0 0 1 0 0 0
# LUI  rd, imm20  (RV32I: load upper 20 bits)
0x19 0x00 0x00 0 0 11 0 6 1 0 0 0 0 0 0 0 0 1 0 0 0
# AUIPC rd, imm20 (PC + upper imm)
0x1A 0x96 0x05 0 0 11 0 0 1 0 0 0 0 0 0 0 1 1 3 0 0
# MOVT rd, imm16  (upper 16 placement — ARM MOVT style)
0x1B 0x00 0x00 0 0 10 0 6 1 0 0 0 0 0 0 0 0 1 0 0 0
# MOVI rd, imm8s  (quick small constant load)
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*/
