// Digital circuit mul-div.dig as structural Verilog
module mul_div (
  input  [31:0] B,
  input  [1:0] mode,
  input  clk,
  input  load,
  input  [15:0] A,
  output [31:0] bout,
  output [31:0] Out,
  output [3:0] steps
);

  wire add_en, decoder_1_out_0, decoder_1_out_1, decoder_1_out_2, decoder_1_out_3, decoder_1_out_4,
       decoder_1_out_5, decoder_1_out_6, decoder_1_out_7, decoder_1_out_8, decoder_1_out_9, decoder_1_out_10,
       decoder_1_out_11, decoder_1_out_12, decoder_1_out_13, decoder_1_out_14, decoder_1_out_15;
  wire [3:0] enc_out;
  wire [15:0] d0, d1, multiplexer_2_out, new_enc;
  wire [31:0] add_1_s, multiplexer_1_out, register_1_q, shift_1_out;

  assign d1 = new_enc & d0;  // And and_1, 16 bits wide
  not not_1 (new_enc[0], decoder_1_out_0);
  not not_2 (new_enc[1], decoder_1_out_1);
  Decoder #(.Selector_Bits(4)) decoder_1 (
    .sel(enc_out), .out_0(decoder_1_out_0), .out_1(decoder_1_out_1), .out_2(decoder_1_out_2),
    .out_3(decoder_1_out_3), .out_4(decoder_1_out_4), .out_5(decoder_1_out_5), .out_6(decoder_1_out_6),
    .out_7(decoder_1_out_7), .out_8(decoder_1_out_8), .out_9(decoder_1_out_9), .out_10(decoder_1_out_10),
    .out_11(decoder_1_out_11), .out_12(decoder_1_out_12), .out_13(decoder_1_out_13),
    .out_14(decoder_1_out_14), .out_15(decoder_1_out_15));
  PriorityEncoder #(.Selector_Bits(4)) priorityencoder_1 (
    .in0(d0[0]), .in1(d0[1]), .in2(d0[2]), .in3(d0[3]), .in4(d0[4]), .in5(d0[5]), .in6(d0[6]), .in7(d0[7]),
    .in8(d0[8]), .in9(d0[9]), .in10(d0[10]), .in11(d0[11]), .in12(d0[12]), .in13(d0[13]), .in14(d0[14]),
    .in15(d0[15]), .num(enc_out));  // open: any
  not not_3 (new_enc[2], decoder_1_out_2);
  not not_4 (new_enc[3], decoder_1_out_3);
  not not_5 (new_enc[4], decoder_1_out_4);
  not not_6 (new_enc[5], decoder_1_out_5);
  shift shift_1 (.A({{16{1'b0}}, B[15:0]}), .mode(mode), .B({{28{1'b0}}, enc_out}), .Out(shift_1_out));
  not not_7 (new_enc[6], decoder_1_out_6);
  not not_8 (new_enc[7], decoder_1_out_7);
  not not_9 (new_enc[8], decoder_1_out_8);
  not not_10 (new_enc[9], decoder_1_out_9);
  not not_11 (new_enc[10], decoder_1_out_10);
  not not_12 (new_enc[11], decoder_1_out_11);
  not not_13 (new_enc[12], decoder_1_out_12);
  not not_14 (new_enc[13], decoder_1_out_13);
  not not_15 (new_enc[14], decoder_1_out_14);
  not not_16 (new_enc[15], decoder_1_out_15);
  Multiplexer #(.Bits(32)) multiplexer_1 (.sel(add_en), .in_0({32{1'b0}}), .in_1(shift_1_out), .out(multiplexer_1_out));
  Register #(.Bits(32)) register_1 (.D(Out), .C(clk), .en(add_en), .Q(register_1_q));
  Multiplexer #(.Bits(16)) multiplexer_2 (.sel(load), .in_0(d1), .in_1(A), .out(multiplexer_2_out));
  Add #(.Bits(32)) add_1 (.a(multiplexer_1_out), .b(register_1_q), .c_i(1'b0), .s(add_1_s));  // open: c_o
  or or_1 (add_en, enc_out[0], enc_out[1], enc_out[2], enc_out[3]);
  D_FF #(.Bits(16)) d_ff_1 (.D(multiplexer_2_out), .C(clk), .Q(d0));  // open: nQ
  Multiplexer #(.Bits(32)) multiplexer_3 (.sel(load), .in_0(add_1_s), .in_1({32{1'b0}}), .out(Out));
  Counter #(.Bits(4)) counter_1 (.en(add_en), .C(clk), .clr(load), .out(steps));  // open: ovf

  assign bout = {{16{1'b0}}, B[15:0]};

  // Notes on the sheet:
  //   B: default 50000
  //   mode: default 1
  //   A: default 30000
endmodule
