// Digital circuit program-counter.dig as structural Verilog
module program_counter (
  input  [31:0] mem_din,
  input  [31:0] alu_in,
  input  [2:0] pc_src,
  input  LOAD,
  input  [21:0] IR_ABS,
  input  RESET,
  input  [1:0] cycles,
  input  clk,
  input  FLAG_N,
  input  FLAG_C,
  input  FLAG_Z,
  input  FLAG_V,
  input  [2:0] COND,
  input  jump_type,
  input  branch_en,
  output [23:0] PC_OUT,
  output [23:0] PC_SAVE,
  output FETCH,
  output EXECUTE,
  output MEM_WAIT,
  output COND_RESULT
);

  wire match, mux0, mux1, mux2, MUX_Y, nor_4_out, not_1_out, not_2_out, not_3_out, not_4_out, not_5_out,
       not_6_out, not_7_out, or_4_out, pc_load, pc_reg_en, seq0, seq1, seq_rst, xnor_1_out, xnor_2_out;
  wire [23:0] multiplexer_1_out, pc_mux, pc_rel;
  wire [23:22] ir_abs_x;

  BitExtender #(.inputBits(1), .outputBits(2)) bitextender_1 (.in(IR_ABS[21]), .out(ir_abs_x));
  Multiplexer #(.Bits(24)) multiplexer_1 (.sel(RESET), .in_0(pc_mux), .in_1({24{1'b0}}), .out(multiplexer_1_out));
  or or_1 (mux0, FETCH, pc_src[0]);
  or or_2 (mux1, FETCH, pc_src[1]);
  or or_3 (pc_reg_en, FETCH, pc_load);
  or or_4 (or_4_out, jump_type, COND_RESULT);
  Add #(.Bits(24)) add_1 (.a({ir_abs_x, IR_ABS}), .b(PC_OUT), .c_i(1'b0), .s(pc_rel));  // open: c_o
  Add #(.Bits(24)) add_2 (.a(24'h1), .b(PC_OUT), .c_i(1'b0), .s(PC_SAVE));  // open: c_o
  Register #(.Bits(24)) register_1 (.D(multiplexer_1_out), .C(clk), .en(pc_reg_en), .Q(PC_OUT));
  Multiplexer #(.Selector_Bits(3), .Bits(24)) multiplexer_2 (
    .sel({mux2, mux1, mux0}), .in_0({2'b00, IR_ABS}), .in_1(pc_rel), .in_2({24{1'b0}}), .in_3({24{1'b0}}),
    .in_4(alu_in[23:0]), .in_5(mem_din[23:0]), .in_6({24{1'b0}}), .in_7(PC_SAVE), .out(pc_mux));
  and and_1 (pc_load, EXECUTE, or_4_out);
  or or_5 (mux2, FETCH, pc_src[2]);
  and and_2 (COND_RESULT, MUX_Y, branch_en);
  Multiplexer #(.Selector_Bits(3)) multiplexer_3 (
    .sel(COND), .in_0(FLAG_Z), .in_1(FLAG_C), .in_2(FLAG_N), .in_3(FLAG_V), .in_4(not_1_out),
    .in_5(not_2_out), .in_6(not_3_out), .in_7(not_4_out), .out(MUX_Y));
  not not_1 (not_1_out, FLAG_Z);
  not not_2 (not_2_out, FLAG_C);
  not not_3 (not_3_out, FLAG_N);
  not not_4 (not_4_out, FLAG_V);
  not not_5 (not_5_out, clk);
  Counter #(.Bits(2)) counter_1 (.en(1'b1), .C(not_5_out), .clr(seq_rst), .out({seq1, seq0}));  // open: ovf
  nor nor_1 (FETCH, seq0, seq1);
  nor nor_2 (EXECUTE, not_6_out, seq1);
  not not_6 (not_6_out, seq0);
  nor nor_3 (MEM_WAIT, seq0, not_7_out);
  not not_7 (not_7_out, seq1);
  xnor xnor_1 (xnor_1_out, cycles[0], seq0);
  xnor xnor_2 (xnor_2_out, cycles[1], seq1);
  nor nor_4 (nor_4_out, match, RESET);
  not not_8 (seq_rst, nor_4_out);
  and and_3 (match, xnor_1_out, xnor_2_out);

  // Other names for the same wires on the sheet: alu[23:0] = alu_in[23:0]; brch_en = branch_en; cyc0 = cycles[0];
  //   cyc1 = cycles[1]; ir_abs_t[21:0] = IR_ABS; ir_abs_x[21:0] = IR_ABS; jmp_type = jump_type;
  //   mem_in[23:0] = mem_din[23:0]; seq_out[1:0] = {seq1, seq0}

  // Notes on the sheet:
  //   IR_ABS: default 1
  //   INPUTS
  //   OUTPUTS
  //   BRANCH
  //   SEQUENCER
endmodule

/* Test case branch-pc:
clk cycles jump-type branch-en RESET pc-src IR_ABS alu-in mem-din FLAG_Z FLAG_C FLAG_N FLAG_V COND PC-OUT PC-SAVE

# Branch PC integration — BEQ/BNE in EXEC (cycles=1), pc-src=1 relative

# RESET hold
0 0 0 0 1 0 0 0 0 0 0 0 0 0 x x
C 0 0 0 1 0 0 0 0 0 0 0 0 0 0 1
0 0 0 0 1 0 0 0 0 0 0 0 0 0 0 1

# Release RESET, first FETCH
0 0 0 0 0 0 0 0 0 0 0 0 0 0 x x
C 0 0 0 0 0 0 0 0 0 0 0 0 0 1 2
0 0 0 0 0 0 0 0 0 0 0 0 0 0 1 2

# Enter EXEC (cycles=1)
0 1 0 0 0 0 0x3FFF 0 0 0 0 0 0 0 1 2
C 1 0 0 0 0 0x3FFF 0 0 0 0 0 0 0 2 3
0 1 0 0 0 0 0x3FFF 0 0 0 0 0 0 0 2 3

# Absolute jump to PC=0x51 in EXEC
0 1 1 0 0 0 0x51 0 0 0 0 0 0 0 x x
C 1 1 0 0 0 0x51 0 0 0 0 0 0 0 0x51 0x52
0 1 1 0 0 0 0x51 0 0 0 0 0 0 0 0x51 0x52

# FETCH->EXEC (PC 0x51->0x52)
0 1 0 0 0 0 0x3FFF 0 0 0 0 0 0 0 0x51 0x52
C 1 0 0 0 0 0x3FFF 0 0 0 0 0 0 0 0x52 0x53
0 1 0 0 0 0 0x3FFF 0 0 0 0 0 0 0 0x52 0x53

# BEQ taken (Z=1, COND=0): PC=0x52 + (-4) = 0x4E
0 1 0 1 0 1 0x3FFFFC 0 0 1 0 0 0 0 x x
C 1 0 1 0 1 0x3FFFFC 0 0 1 0 0 0 0 0x4E 0x4F
0 1 0 1 0 1 0x3FFFFC 0 0 1 0 0 0 0 0x4E 0x4F

# FETCH->EXEC after BEQ (jump only works in EXEC)
0 1 0 0 0 0 0x3FFF 0 0 0 0 0 0 0 0x4E 0x4F
C 1 0 0 0 0 0x3FFF 0 0 0 0 0 0 0 0x4F 0x50
0 1 0 0 0 0 0x3FFF 0 0 0 0 0 0 0 0x4F 0x50

# Jump back to 0x52 in EXEC
0 1 1 0 0 0 0x52 0 0 0 0 0 0 0 x x
C 1 1 0 0 0 0x52 0 0 0 0 0 0 0 0x52 0x53
0 1 0 0 0 0 0x3FFF 0 0 0 0 0 0 0 0x52 0x53
C 1 0 0 0 0 0x3FFF 0 0 0 0 0 0 0 0x53 0x54

# BEQ not taken (Z=0): PC stays 0x53
0 1 0 1 0 1 0x3FFFFC 0 0 0 0 0 0 0 x x
C 1 0 1 0 1 0x3FFFFC 0 0 0 0 0 0 0 0x53 0x54
0 1 0 1 0 1 0x3FFFFC 0 0 0 0 0 0 0 0x53 0x54

# FETCH->EXEC after BEQ not taken
0 1 0 0 0 0 0x3FFF 0 0 0 0 0 0 0 0x53 0x54
C 1 0 0 0 0 0x3FFF 0 0 0 0 0 0 0 0x54 0x55
0 1 0 0 0 0 0x3FFF 0 0 0 0 0 0 0 0x54 0x55

# Jump to 0x56 for BNE test (EXEC)
0 1 1 0 0 0 0x56 0 0 0 0 0 0 0 x x
C 1 1 0 0 0 0x56 0 0 0 0 0 0 0 0x56 0x57
0 1 0 0 0 0 0x3FFF 0 0 0 0 0 0 0 0x56 0x57
C 1 0 0 0 0 0x3FFF 0 0 0 0 0 0 0 0x57 0x58

# BNE taken (Z=0, COND=4 ~Z): PC=0x57 + (-4) = 0x53
0 1 0 1 0 1 0x3FFFFC 0 0 0 0 0 0 4 x x
C 1 0 1 0 1 0x3FFFFC 0 0 0 0 0 0 4 0x53 0x54
0 1 0 1 0 1 0x3FFFFC 0 0 0 0 0 0 4 0x53 0x54
*/

/* Test case branch:
FLAG_Z FLAG_C FLAG_N FLAG_V COND branch-en COND_RESULT

# Branch condition mux (74151) + branch-en gate; combinational


# 1. Plan milestone cases

1 0 0 0 0 1 1
1 0 0 0 4 1 0
1 0 0 0 0 0 0
0 1 0 0 1 1 1
0 0 0 0 4 1 1

# 2. All eight conditions — taken, not-taken, BRANCH_EN gate

1 0 0 0 0 1 1
1 0 0 0 0 0 0
0 1 0 0 1 1 1
0 1 0 0 1 0 0
0 0 1 0 2 1 1
0 0 1 0 2 0 0
0 0 0 1 3 1 1
0 0 0 1 3 0 0
0 0 0 0 4 1 1
0 0 0 0 4 0 0
0 0 0 0 5 1 1
0 0 0 0 5 0 0
0 0 0 0 6 1 1
0 0 0 0 6 0 0
0 0 0 0 7 1 1
0 0 0 0 7 0 0
0 0 0 0 0 1 0
0 0 0 0 1 1 0
0 0 0 0 2 1 0
0 0 0 0 3 1 0
1 0 0 0 4 1 0
0 1 0 0 5 1 0
0 0 1 0 6 1 0
0 0 0 1 7 1 0

# 3. Cross-condition — wrong flag for opcode

0 1 0 0 0 1 0
1 0 0 0 1 1 0

# 4. Inverted conditions vs direct (JZ vs JNZ)

1 0 0 0 0 1 1
1 0 0 0 4 1 0
0 0 0 0 4 1 1
0 0 0 0 0 1 0

# 5. Complete truth table — 2^8 inputs (all flags × cond × BRANCH_EN)

0 0 0 0 0 0 0
0 0 0 0 0 1 0
0 0 0 1 0 0 0
0 0 0 1 0 1 0
0 0 1 0 0 0 0
0 0 1 0 0 1 0
0 0 1 1 0 0 0
0 0 1 1 0 1 0
0 1 0 0 0 0 0
0 1 0 0 0 1 0
0 1 0 1 0 0 0
0 1 0 1 0 1 0
0 1 1 0 0 0 0
0 1 1 0 0 1 0
0 1 1 1 0 0 0
0 1 1 1 0 1 0
1 0 0 0 0 0 0
1 0 0 0 0 1 1
1 0 0 1 0 0 0
1 0 0 1 0 1 1
1 0 1 0 0 0 0
1 0 1 0 0 1 1
1 0 1 1 0 0 0
1 0 1 1 0 1 1
1 1 0 0 0 0 0
1 1 0 0 0 1 1
1 1 0 1 0 0 0
1 1 0 1 0 1 1
1 1 1 0 0 0 0
1 1 1 0 0 1 1
1 1 1 1 0 0 0
1 1 1 1 0 1 1
0 0 0 0 1 0 0
0 0 0 0 1 1 0
0 0 0 1 1 0 0
0 0 0 1 1 1 0
0 0 1 0 1 0 0
0 0 1 0 1 1 0
0 0 1 1 1 0 0
0 0 1 1 1 1 0
0 1 0 0 1 0 0
0 1 0 0 1 1 1
0 1 0 1 1 0 0
0 1 0 1 1 1 1
0 1 1 0 1 0 0
0 1 1 0 1 1 1
0 1 1 1 1 0 0
0 1 1 1 1 1 1
1 0 0 0 1 0 0
1 0 0 0 1 1 0
1 0 0 1 1 0 0
1 0 0 1 1 1 0
1 0 1 0 1 0 0
1 0 1 0 1 1 0
1 0 1 1 1 0 0
1 0 1 1 1 1 0
1 1 0 0 1 0 0
1 1 0 0 1 1 1
1 1 0 1 1 0 0
1 1 0 1 1 1 1
1 1 1 0 1 0 0
1 1 1 0 1 1 1
1 1 1 1 1 0 0
1 1 1 1 1 1 1
0 0 0 0 2 0 0
0 0 0 0 2 1 0
0 0 0 1 2 0 0
0 0 0 1 2 1 0
0 0 1 0 2 0 0
0 0 1 0 2 1 1
0 0 1 1 2 0 0
0 0 1 1 2 1 1
0 1 0 0 2 0 0
0 1 0 0 2 1 0
0 1 0 1 2 0 0
0 1 0 1 2 1 0
0 1 1 0 2 0 0
0 1 1 0 2 1 1
0 1 1 1 2 0 0
0 1 1 1 2 1 1
1 0 0 0 2 0 0
1 0 0 0 2 1 0
1 0 0 1 2 0 0
1 0 0 1 2 1 0
1 0 1 0 2 0 0
1 0 1 0 2 1 1
1 0 1 1 2 0 0
1 0 1 1 2 1 1
1 1 0 0 2 0 0
1 1 0 0 2 1 0
1 1 0 1 2 0 0
1 1 0 1 2 1 0
1 1 1 0 2 0 0
1 1 1 0 2 1 1
1 1 1 1 2 0 0
1 1 1 1 2 1 1
0 0 0 0 3 0 0
0 0 0 0 3 1 0
0 0 0 1 3 0 0
0 0 0 1 3 1 1
0 0 1 0 3 0 0
0 0 1 0 3 1 0
0 0 1 1 3 0 0
0 0 1 1 3 1 1
0 1 0 0 3 0 0
0 1 0 0 3 1 0
0 1 0 1 3 0 0
0 1 0 1 3 1 1
0 1 1 0 3 0 0
0 1 1 0 3 1 0
0 1 1 1 3 0 0
0 1 1 1 3 1 1
1 0 0 0 3 0 0
1 0 0 0 3 1 0
1 0 0 1 3 0 0
1 0 0 1 3 1 1
1 0 1 0 3 0 0
1 0 1 0 3 1 0
1 0 1 1 3 0 0
1 0 1 1 3 1 1
1 1 0 0 3 0 0
1 1 0 0 3 1 0
1 1 0 1 3 0 0
1 1 0 1 3 1 1
1 1 1 0 3 0 0
1 1 1 0 3 1 0
1 1 1 1 3 0 0
1 1 1 1 3 1 1
0 0 0 0 4 0 0
0 0 0 0 4 1 1
0 0 0 1 4 0 0
0 0 0 1 4 1 1
0 0 1 0 4 0 0
0 0 1 0 4 1 1
0 0 1 1 4 0 0
0 0 1 1 4 1 1
0 1 0 0 4 0 0
0 1 0 0 4 1 1
0 1 0 1 4 0 0
0 1 0 1 4 1 1
0 1 1 0 4 0 0
0 1 1 0 4 1 1
0 1 1 1 4 0 0
0 1 1 1 4 1 1
1 0 0 0 4 0 0
1 0 0 0 4 1 0
1 0 0 1 4 0 0
1 0 0 1 4 1 0
1 0 1 0 4 0 0
1 0 1 0 4 1 0
1 0 1 1 4 0 0
1 0 1 1 4 1 0
1 1 0 0 4 0 0
1 1 0 0 4 1 0
1 1 0 1 4 0 0
1 1 0 1 4 1 0
1 1 1 0 4 0 0
1 1 1 0 4 1 0
1 1 1 1 4 0 0
1 1 1 1 4 1 0
0 0 0 0 5 0 0
0 0 0 0 5 1 1
0 0 0 1 5 0 0
0 0 0 1 5 1 1
0 0 1 0 5 0 0
0 0 1 0 5 1 1
0 0 1 1 5 0 0
0 0 1 1 5 1 1
0 1 0 0 5 0 0
0 1 0 0 5 1 0
0 1 0 1 5 0 0
0 1 0 1 5 1 0
0 1 1 0 5 0 0
0 1 1 0 5 1 0
0 1 1 1 5 0 0
0 1 1 1 5 1 0
1 0 0 0 5 0 0
1 0 0 0 5 1 1
1 0 0 1 5 0 0
1 0 0 1 5 1 1
1 0 1 0 5 0 0
1 0 1 0 5 1 1
1 0 1 1 5 0 0
1 0 1 1 5 1 1
1 1 0 0 5 0 0
1 1 0 0 5 1 0
1 1 0 1 5 0 0
1 1 0 1 5 1 0
1 1 1 0 5 0 0
1 1 1 0 5 1 0
1 1 1 1 5 0 0
1 1 1 1 5 1 0
0 0 0 0 6 0 0
0 0 0 0 6 1 1
0 0 0 1 6 0 0
0 0 0 1 6 1 1
0 0 1 0 6 0 0
0 0 1 0 6 1 0
0 0 1 1 6 0 0
0 0 1 1 6 1 0
0 1 0 0 6 0 0
0 1 0 0 6 1 1
0 1 0 1 6 0 0
0 1 0 1 6 1 1
0 1 1 0 6 0 0
0 1 1 0 6 1 0
0 1 1 1 6 0 0
0 1 1 1 6 1 0
1 0 0 0 6 0 0
1 0 0 0 6 1 1
1 0 0 1 6 0 0
1 0 0 1 6 1 1
1 0 1 0 6 0 0
1 0 1 0 6 1 0
1 0 1 1 6 0 0
1 0 1 1 6 1 0
1 1 0 0 6 0 0
1 1 0 0 6 1 1
1 1 0 1 6 0 0
1 1 0 1 6 1 1
1 1 1 0 6 0 0
1 1 1 0 6 1 0
1 1 1 1 6 0 0
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*/

/* Test case program-counter:
clk cycles jump-type branch-en RESET pc-src IR_ABS alu-in mem-din FLAG_Z FLAG_C FLAG_N FLAG_V COND PC-OUT PC-SAVE

# PC smoke (cycles=0 FETCH / cycles=1 EXEC). RESET=1 hold / RESET=0 run.
# Jumps: jump-type=1 in EXEC. Branches: branch-en=1, jump-type=0, flags+COND.

# 1. Idle
0 0 0 0 0 0 0 0 0 0 0 0 0 0 0 1

# 2. RESET hold clears PC
0 0 0 0 1 0 0 0 0 0 0 0 0 0 x x
C 0 0 0 1 0 0 0 0 0 0 0 0 0 0 1
0 0 0 0 1 0 0 0 0 0 0 0 0 0 0 1

# 3. Release RESET: first FETCH edge PC 0->1
0 0 0 0 0 0 0 0 0 0 0 0 0 0 x x
C 0 0 0 0 0 0 0 0 0 0 0 0 0 1 2
0 0 0 0 0 0 0 0 0 0 0 0 0 0 1 2

# 4. Second FETCH
C 0 0 0 0 0 0 0 0 0 0 0 0 0 2 3
0 0 0 0 0 0 0 0 0 0 0 0 0 0 2 3

# 5. cycles=1: enter EXEC (last FETCH bumps PC 2->3)
0 1 0 0 0 0 0x3FFF 0 0 0 0 0 0 0 2 3
C 1 0 0 0 0 0x3FFF 0 0 0 0 0 0 0 3 4
0 1 0 0 0 0 0x3FFF 0 0 0 0 0 0 0 3 4

# 6. Absolute jump (EXEC + jump-type)
0 1 1 0 0 0 0x50 0 0 0 0 0 0 0 x x
C 1 1 0 0 0 0x50 0 0 0 0 0 0 0 0x50 0x51
0 1 1 0 0 0 0x50 0 0 0 0 0 0 0 0x50 0x51

# FETCH->EXEC setup for next jump
0 1 0 0 0 0 0x3FFF 0 0 0 0 0 0 0 0x50 0x51
C 1 0 0 0 0 0x3FFF 0 0 0 0 0 0 0 0x51 0x52
0 1 0 0 0 0 0x3FFF 0 0 0 0 0 0 0 0x51 0x52

# 7. PC-relative jump (0x51 - 4 = 0x4D)
0 1 1 0 0 1 0x3FFFFC 0 0 0 0 0 0 0 x x
C 1 1 0 0 1 0x3FFFFC 0 0 0 0 0 0 0 0x4D 0x4E
0 1 1 0 0 1 0x3FFFFC 0 0 0 0 0 0 0 0x4D 0x4E

# FETCH->EXEC setup for ALU jump
0 1 0 0 0 0 0x3FFF 0 0 0 0 0 0 0 0x4D 0x4E
C 1 0 0 0 0 0x3FFF 0 0 0 0 0 0 0 0x4E 0x4F
0 1 0 0 0 0 0x3FFF 0 0 0 0 0 0 0 0x4E 0x4F

# 8. ALU jump
0 1 1 0 0 4 0 0x200 0 0 0 0 0 0 x x
C 1 1 0 0 4 0 0x200 0 0 0 0 0 0 0x200 0x201
0 1 1 0 0 4 0 0x200 0 0 0 0 0 0 0x200 0x201

# 9. RESET forces PC=0
0 0 0 0 1 0 0 0 0 0 0 0 0 0 x x
C 0 0 0 1 0 0 0 0 0 0 0 0 0 0 1
0 0 0 0 1 0 0 0 0 0 0 0 0 0 0 1

# 10. FETCH after RESET release
0 0 0 0 0 0 0 0 0 0 0 0 0 0 x x
C 0 0 0 0 0 0 0 0 0 0 0 0 0 1 2
0 0 0 0 0 0 0 0 0 0 0 0 0 0 1 2

# 11. Leave sequencer in RESET hold for sequencer-exhaustive
0 0 0 0 1 0 0 0 0 0 0 0 0 0 x x
C 0 0 0 1 0 0 0 0 0 0 0 0 0 0 1
0 0 0 0 1 0 0 0 0 0 0 0 0 0 0 1
*/

/* Test case sequencer:
RESET cycles clk FETCH EXECUTE MEM-WAIT

# From sequencer.dig; RESET active-high hold (invert main reset)
# RESET=1 hold, RESET=0 run

# Sync after prog-count-2-smoke (phase may not be FETCH)
1 0 C x x x

# Hold (RESET=1): counter cleared — FETCH
1 0 0 1 0 0
1 0 C 1 0 0

# Release run (RESET=0), cycles=0: single-phase (FETCH only)
0 0 0 1 0 0
0 0 C 1 0 0
0 0 C 1 0 0

# cycles=1: FETCH -> EXECUTE -> FETCH (2 phases)
0 1 0 1 0 0
0 1 C 0 1 0
0 1 C 1 0 0
0 1 C 0 1 0
0 1 C 1 0 0

# cycles=2: FETCH -> EXECUTE -> MEM_WAIT -> FETCH (3 phases)
0 2 0 1 0 0
0 2 C 0 1 0
0 2 C 0 0 1
0 2 C 1 0 0
0 2 C 0 1 0
0 2 C 0 0 1
0 2 C 1 0 0

# cycles=3: four counter steps — terminal reload at 11
0 3 0 1 0 0
0 3 C 0 1 0
0 3 C 0 0 1
0 3 C 0 0 0
0 3 C 1 0 0

# Run hold: RESET=1 clears counter (FETCH)
0 2 C 0 1 0
1 2 0 0 1 0
1 2 C 1 0 0
0 2 C 0 1 0

# Mid-flight cycles change
1 0 C 1 0 0
0 1 C 0 1 0
0 2 0 0 1 0
0 2 C 0 0 1
0 2 C 1 0 0

# cycles=0 lock: never leaves FETCH
1 0 C 1 0 0
0 0 C 1 0 0
0 0 C 1 0 0
0 0 C 1 0 0
*/
