// Digital circuit register.dig as structural Verilog
module register (
  input  WE,
  input  [31:0] DATA_W,
  input  [7:0] ADDR_A,
  input  [7:0] ADDR_B,
  input  [7:0] ADDR_W,
  input  EXEC,
  input  addr_c_sel,
  input  [31:0] ir_bus,
  input  clk,
  output [31:0] DATA_A,
  output [31:0] DATA_B,
  output [31:0] DATA_C
);

  wire ram_and;
  wire [7:0] ADDR_C;

  RAMDualAccess #(.AddrBits(8), .Bits(32)) U1 (
    .str(ram_and), .C(clk), .ld(1'b1), .A1(ADDR_W), .Din1(DATA_W), .A2(ADDR_A), .D2(DATA_A));  // open: D1
  and and_1 (ram_and, EXEC, WE);
  RAMDualAccess #(.AddrBits(8), .Bits(32)) U2 (
    .str(ram_and), .C(clk), .ld(1'b1), .A1(ADDR_W), .Din1(DATA_W), .A2(ADDR_B), .D2(DATA_B));  // open: D1
  RAMDualAccess #(.AddrBits(8), .Bits(32)) U3 (
    .str(ram_and), .C(clk), .ld(1'b1), .A1(ADDR_W), .Din1(DATA_W), .A2(ADDR_C), .D2(DATA_C));  // open: D1
  Multiplexer #(.Bits(8)) multiplexer_1 (.sel(addr_c_sel), .in_0({8{1'b0}}), .in_1(ir_bus[23:16]), .out(ADDR_C));

  // Other names for the same wires on the sheet: IR_ADDR_CIN[7:0] = ir_bus[23:16]
endmodule

/* Test case regfile-exhaustive:
clk WE EXEC DATA_W ADDR_A ADDR_B ADDR_W addr_c_sel IR_ADDR_CIN DATA_A DATA_B DATA_C
# 1. Unwritten memory reads as zero (combinational)
0 0 0 0x00000000 0 0 0 0 0 0x00000000 0x00000000 0x00000000
0 0 0 0x00000000 1 2 0 1 0x2A 0x00000000 0x00000000 0x00000000
0 0 0 0x00000000 0xFF 0x80 0 0 0 0x00000000 0x00000000 0x00000000
# 2. WRITE_REG — EXEC=1 WE=1 on clk posedge
0 1 1 0x0000ABCD 0 0 1 0 0 x x x
C 1 1 0x0000ABCD 0 0 1 0 0 x x x
0 1 1 0x0000ABCD 0 0 1 0 0 x x x
0 0 0 0x00000000 1 1 0 1 1 0x0000ABCD 0x0000ABCD 0x0000ABCD
0 1 1 0xDEADBEEF 0 0 7 0 0 x x x
C 1 1 0xDEADBEEF 0 0 7 0 0 x x x
0 1 1 0xDEADBEEF 0 0 7 0 0 x x x
0 0 0 0x00000000 7 7 0 1 7 0xDEADBEEF 0xDEADBEEF 0xDEADBEEF
# 3. WE=0 — no write on posedge
0 0 1 0x11111111 0 0 10 0 0 x x x
C 0 1 0x11111111 0 0 10 0 0 x x x
0 0 1 0x11111111 0 0 10 0 0 x x x
0 0 0 0x00000000 10 10 0 0 0 0x00000000 0x00000000 0x00000000
0 1 1 0x22222222 0 0 10 0 0 x x x
C 1 1 0x22222222 0 0 10 0 0 x x x
0 1 1 0x22222222 0 0 10 0 0 x x x
0 0 0 0x00000000 10 10 0 0 0 0x22222222 0x22222222 0x00000000
# 4. EXEC=0 — no write on posedge
0 1 0 0x33333333 0 0 11 0 0 x x x
C 1 0 0x33333333 0 0 11 0 0 x x x
0 1 0 0x33333333 0 0 11 0 0 x x x
0 0 0 0x00000000 11 11 0 0 0 0x00000000 0x00000000 0x00000000
0 1 1 0x44444444 0 0 11 0 0 x x x
C 1 1 0x44444444 0 0 11 0 0 x x x
0 1 1 0x44444444 0 0 11 0 0 x x x
0 0 0 0x00000000 11 11 0 0 0 0x44444444 0x44444444 0x00000000
# 5. Write gating matrix (fixed DATA_W on C)
0 0 0 0xA0000000 0x14 0x14 0x14 1 0x14 x x x
C 0 0 0xA0000000 0x14 0x14 0x14 1 0x14 x x x
0 0 0 0xA0000000 0x14 0x14 0x14 1 0x14 0x00000000 0x00000000 0x00000000
0 0 1 0xA0000001 0x15 0x15 0x15 1 0x15 x x x
C 0 1 0xA0000001 0x15 0x15 0x15 1 0x15 x x x
0 0 0 0xA0000001 0x15 0x15 0x15 1 0x15 0x00000000 0x00000000 0x00000000
0 1 0 0xA0000002 0x16 0x16 0x16 1 0x16 x x x
C 1 0 0xA0000002 0x16 0x16 0x16 1 0x16 x x x
0 0 0 0xA0000002 0x16 0x16 0x16 1 0x16 0x00000000 0x00000000 0x00000000
0 1 1 0xA0000003 0x17 0x17 0x17 1 0x17 x x x
C 1 1 0xA0000003 0x17 0x17 0x17 1 0x17 x x x
0 0 0 0xA0000003 0x17 0x17 0x17 1 0x17 0xA0000003 0xA0000003 0xA0000003
# 6. addr_c_sel mux — port C address
0 1 1 0xCAFEBABE 0 0 0x2A 0 0 x x x
C 1 1 0xCAFEBABE 0 0 0x2A 0 0 x x x
0 1 1 0xCAFEBABE 0 0 0x2A 0 0 x x x
0 0 0 0x00000000 1 2 0 0 0x63 0x0000ABCD 0x00000000 0x00000000
0 0 0 0x00000000 1 2 0 1 0x2A 0x0000ABCD 0x00000000 0xCAFEBABE
# 7. Triple-port simultaneous read (different addresses)
0 1 1 0x00000001 0 0 1 0 0 x x x
C 1 1 0x00000001 0 0 1 0 0 x x x
0 1 1 0x00000001 0 0 1 0 0 x x x
0 1 1 0x00000002 0 0 2 0 0 x x x
C 1 1 0x00000002 0 0 2 0 0 x x x
0 1 1 0x00000002 0 0 2 0 0 x x x
0 1 1 0x00000003 0 0 3 0 0 x x x
C 1 1 0x00000003 0 0 3 0 0 x x x
0 1 1 0x00000003 0 0 3 0 0 x x x
0 0 0 0x00000000 1 2 0 1 3 0x00000001 0x00000002 0x00000003
# 8. Overwrite same address
0 1 1 0xAAAAAAAA 0 0 5 0 0 x x x
C 1 1 0xAAAAAAAA 0 0 5 0 0 x x x
0 1 1 0xAAAAAAAA 0 0 5 0 0 x x x
0 0 0 0x00000000 5 5 0 1 5 0xAAAAAAAA 0xAAAAAAAA 0xAAAAAAAA
0 1 1 0x55555555 0 0 5 0 0 x x x
C 1 1 0x55555555 0 0 5 0 0 x x x
0 1 1 0x55555555 0 0 5 0 0 x x x
0 0 0 0x00000000 5 5 0 1 5 0x55555555 0x55555555 0x55555555
# 9. R0 and max index
0 1 1 0x00000001 0 0 0 0 0 x x x
C 1 1 0x00000001 0 0 0 0 0 x x x
0 1 1 0x00000001 0 0 0 0 0 x x x
0 0 0 0x00000000 0 0 0 0 0 0x00000001 0x00000001 0x00000001
0 1 1 0xFFFFFFFF 0 0 0xFF 0 0 x x x
C 1 1 0xFFFFFFFF 0 0 0xFF 0 0 x x x
0 1 1 0xFFFFFFFF 0 0 0xFF 0 0 x x x
0 0 0 0x00000000 0xFF 0xFF 0 1 0xFF 0xFFFFFFFF 0xFFFFFFFF 0xFFFFFFFF
# 10. Read does not require EXEC or WE
0 0 0 0x00000000 3 3 0 1 3 0x00000003 0x00000003 0x00000003
# 11. Write ADDR_W independent of read addresses
0 1 1 0x0BADF00D 0 0 0x63 0 0 x x x
C 1 1 0x0BADF00D 0 0 0x63 0 0 x x x
0 1 1 0x0BADF00D 0 0 0x63 0 0 x x x
0 0 0 0x00000000 1 2 0 1 0x63 0x00000001 0x00000002 0x0BADF00D
*/
