// Digital circuit vga.dig as structural Verilog
module vga (
  input  [23:0] mem_addr,
  input  [31:0] mem_din,
  input  [12:0] disp_read_addr,
  input  clk,
  output [31:0] disp_data_out
);

  wire not_1_out, vga_en;

  and and_1 (vga_en, not_1_out, mem_addr[20], mem_addr[21]);
  not not_1 (not_1_out, mem_addr[19]);
  RAMDualAccess #(.AddrBits(13), .Bits(16)) ramdualaccess_1 (
    .str(vga_en), .C(clk), .ld(1'b1), .A1(mem_addr[12:0]), .Din1(mem_din[31:16]), .A2(disp_read_addr),
    .D2(disp_data_out[15:0]));  // open: D1
  RAMDualAccess #(.AddrBits(13), .Bits(16)) ramdualaccess_2 (
    .str(vga_en), .C(clk), .ld(1'b1), .A1(mem_addr[12:0]), .Din1(mem_din[15:0]), .A2(disp_read_addr),
    .D2(disp_data_out[31:16]));  // open: D1

  // Other names for the same wires on the sheet: disp_write_addr[12:0] = mem_addr[12:0];
  //   disp_data_in0[15:0] = mem_din[15:0]; disp_data_in1[15:0] = mem_din[31:16]

  // Notes on the sheet:
  //   mem_addr: default 3145728
endmodule

/* Test case vga-tile-write-read:
mem_addr mem_din disp-read-addr clk disp-data-out

# Tile RAM: CPU write port A, scan-out read port B. disp-data-out = {lo16, hi16}.
0x000000 0x00000000 0 0 0x00000000
0xF10000 0xFFFF0041 0 0 x
0xF10000 0xFFFF0041 0 C 0x41FFFF
0xF10004 0x0000FF42 4 0 x
0xF10004 0x0000FF42 4 C 0xFF420000
0xF10000 0xFFFF0041 0 0 0x41FFFF
*/

/* Test case vga-dual-port-poll:
mem_addr mem_din disp-read-addr clk disp-data-out

# Dual-port: poll read addr 0 while CPU writes addr 4; MMIO addr does not hit tile 0.
0x000000 0x00000000 0 0 0x00000000
0xF10000 0x07E00041 0 0 x
0xF10000 0x07E00041 0 C 0x4107E0
0xF10004 0xF8000042 0 0 0x4107E0
0xF10004 0xF8000042 0 C 0x4107E0
0xF10004 0xF8000042 4 0 0x42F800
0xF10000 0x07E00041 0 0 0x4107E0
0xF00018 0xDEADBEEF 0 0 0x4107E0
0xF00018 0xDEADBEEF 0 C 0x4107E0
*/
